# Fritzing sketch IoT-RPi-Weather-Station (saved by Fritzing 0.9.3b)
breadboards: 1

parts:
  Raspberry_Pi_1 = Raspberry Pi 3 [part_number=RPI-3-V1.2]
  DHT22 = Humidity and Temperature Sensor RHT03 [part_number="TEMP/HUM SENSOR"]
  R5 = Resistor [tolerance=±5% resistance=4.7k package=THT]
  Ext_Temperature_Sensor = DS18B20 1-Wire Temperature Sensor [part_number=DS18B20]
  R6 = Resistor [tolerance=±5% resistance=4.7k package=THT]
  TEMP/PRESS/ALT_Sensor = Barometric Pressure Sensor - BMP180 Breakout (GY-68)

nets:
  VCC: Raspberry_Pi_1.3v3, DHT22.Vcc, R5.Pin_0, Ext_Temperature_Sensor.VDD, R6.Pin_0, TEMP/PRESS/ALT_Sensor.VCC
  N1: Raspberry_Pi_1.GPIO2, TEMP/PRESS/ALT_Sensor.SDA
  N2: Raspberry_Pi_1.GPIO3, TEMP/PRESS/ALT_Sensor.SCL
  N3: Raspberry_Pi_1.GIPO4, Ext_Temperature_Sensor.DQ, R6.Pin_1
  N4: Raspberry_Pi_1.GIPO16, DHT22.Data-signal, R5.Pin_1
  GND: DHT22.GND_2, Ext_Temperature_Sensor.GND, TEMP/PRESS/ALT_Sensor.GND

notes:
  3.3V
  GPIO 16
  GPIO 4
  GPIO 2 - SDA
  GPIO 3 - SCL
